# Fritzing sketch hc-sr04 (saved by Fritzing 0.8.7b)
breadboards: 1

parts:
  Part1 = SRF05 Ultrasonic Rangefinder
  Arduino1 = Arduino Uno (Rev3)

nets:
  N1: Part1.Trig, Part1.Echo, Arduino1.D7
  GND: Part1.GND, Arduino1.GND
