# Fritzing sketch led-rainbow (saved by Fritzing 0.7.12b)
breadboards: 1

parts:
  Arduino1 = Arduino
  LED1 = RGB LED (com. anode, rbg) [package="5 mm [THT]"]

nets:
  N1: Arduino1.GND, LED1.common_anode
  N2: Arduino1.D6, LED1.green_cathode
  N3: Arduino1.D5, LED1.blue_cathode
  N4: Arduino1.D3, LED1.red_cathode
