# Fritzing sketch led-rgb-anode (saved by Fritzing 0.9.0b)
breadboards: 1

parts:
  Part1 = Arduino Uno (Rev3)
  R1 = Resistor [tolerance=±5% resistance=220 package=THT]
  LED2 = RGB LED (com. anode, rbg) [package="5 mm [THT]"]

nets:
  N1: Part1.D3_PWM, LED2.red_cathode
  N2: Part1.D5_PWM, LED2.blue_cathode
  N3: Part1.D6_PWM, LED2.green_cathode
  N4: Part1.5V, R1.Pin_0
  N5: R1.Pin_1, LED2.common_anode
