# Fritzing sketch sensor-slider (saved by Fritzing 0.9.1b)

parts:
  Part1 = Arduino Uno (Rev3)
  U2 = SLIDER [package=slider]

nets:
  N1: Part1.A0, U2.A
  N2: Part1.5V, U2.S
  N3: Part1.GND, U2.E

custom parts:
  SLIDER: Slide-type potentiometer- COM-9119
